# Fritzing sketch Wiring Diagram (saved by Fritzing 0.9.3b)

parts:
  Part1 = Adafruit Trinket 3V [part_number="Adafruit #1500"]
  Part2 = Adafruit LSM303DLHC Triple-axis Accelerometer+Magnetometer (Compass) [part_number="Adafruit #1120"]
  Part3 = NeoPixel Jewel [part_number=2226]
  VCC1 = Battery block 9V

nets:
  N1: Part1.VBAT, VCC1.+
  GND: Part1.GND, Part2.GND, Part3.GND, VCC1.-
  N2: Part1.#4, Part3.IN
  N3: Part1.#0, Part2.SDA
  N4: Part1.#2, Part2.SCL
  +3V3: Part1.+3V3, Part2.VIN, Part3.VDD

custom parts:
  Adafruit Trinket 3V: Trinket may be small, but do not be fooled by its size! It's a tiny microcontroller board, built around the Atmel ATtiny85, a little chip with a lot of power. We wanted to design a microcontroller board that was small enough to fit into any project, and low cost enough to use without hesitation. Perfect for when you don't want to give up your expensive dev-board and you aren't willing to take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
  Adafruit LSM303DLHC Triple-axis Accelerometer+Magnetometer (Compass): He told you "Go West, young maker!" - but you don't know which way is West! Ah, if only you had this triple-axis accelerometer/magnetometer compass module. Inside are two sensors, one is a classic 3-axis accelerometer, which can tell you which direction is down towards the Earth (by measuring gravity). The other is a magnetometer that can sense where the strongest magnetic force is coming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
  NeoPixel Jewel: We fit seven of our tiny 5050 (5mm x 5mm) smart RGB LEDs onto a beautiful, round PCB with mounting holes and a chainable design to create what we think is our most elegant (and evening-wear appropriate) NeoPixel board yet. Use only one microcontroller pin to control as many as you can chain together! Each LED is addressable as the driver chip is inside the LED. Each one has ~18mA constant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
